// Logisim project t-ff-counter.circ as structural Verilog: 1 circuit, main circuit main
module main (
  output out_1,
  output out_2,
  output out_3
);

  wire and_1_out, and_2_out, clock_1_out, or_1_out, or_2_out, t_ff_3_qn;

  and and_1 (and_1_out, out_2, out_3);
  and and_2 (and_2_out, out_1, t_ff_3_qn);
  Clock clock_1 (.out(clock_1_out));
  or or_1 (or_1_out, and_1_out, and_2_out);
  Hex_Digit_Display hex_digit_display_1 (.value({1'b0, out_1, out_2, out_3}));  // open: dp
  T_Flip_Flop t_ff_1 (.clk(clock_1_out), .T(or_1_out), .Q(out_1), .preset(1'b0), .reset(1'b0), .en(1'b1));  // open: Qn
  T_Flip_Flop t_ff_2 (.clk(clock_1_out), .T(or_2_out), .Q(out_2), .preset(1'b0), .reset(1'b0), .en(1'b1));  // open: Qn
  or or_2 (or_2_out, out_2, out_3);
  T_Flip_Flop t_ff_3 (
    .clk(clock_1_out), .T(t_ff_3_qn), .Q(out_3), .Qn(t_ff_3_qn), .preset(1'b0), .reset(1'b0), .en(1'b1));
endmodule
